# Fritzing sketch arduino-wiring (saved by Fritzing 0.9.3b)
breadboards: 1

parts:
  ZS-042_RTC1 = ZS-042 RTC Module
  Part1 = Arduino BT
  NEOPIXEL1 = Neopixel Strip -- White (60/m)

nets:
  GND: ZS-042_RTC1.GND, Part1.GND, NEOPIXEL1.GND
  VCC: ZS-042_RTC1.VCC, Part1.5V, NEOPIXEL1.DI
  N1: ZS-042_RTC1.SDA, Part1.A5/SCL
  N2: ZS-042_RTC1.SCL, Part1.A4/SDA
  N3: Part1.PWM_D5, NEOPIXEL1.+5V

custom parts:
  Neopixel Strip -- White (60/m): Neopixel Strip, White, 60 pixels per meter.
